# Fritzing sketch LCD_Back_Neo_Key_RxTx_emergency_stop (saved by Fritzing 0.9.3b)
breadboards: 1

parts:
  Bauteil1 = Arduino Nano (Rev3.0)
  GLCD_128x1 = 128 x 64 Graphic LCD
  R2 = Resistor [tolerance=±5% resistance=1k package="2010 [SMD]"]
  C1 = Electrolytic Capacitor [capacitance=10μF voltage=50V package="0605 [SMD, electrolytic]"]
  Q1 = NPN-Transistor [package="TO92 [THT]"]
  Keypad4x4 = Keypad Membran 4x4
  R3 = Resistor [tolerance=±5% resistance=1k package="2010 [SMD]"]
  Bauteil4 = 24 NeoPixel Ring [part_number=1586]
  Bauteil5 = Arduino Nano (Rev3.0)
  Part1 = PowerBoost 1000 Basic  # not connected
  S1 = Momentary Switch [package=ksa_sealed_tac_switch]
  K1 = Relay [part_number=FRS1B-S package=THT]
  Q2 = NPN-Transistor [package="TO92 [THT]"]
  R4 = Resistor [tolerance=±5% resistance=1k package="2010 [SMD]"]

nets:
  GND: Bauteil1.GND, GLCD_128x1.1_Vss, GLCD_128x1.15_CS1, C1.-, Q1.E, Bauteil4.GND, Bauteil5.GND, Q2.E
  N1: Bauteil1.D3, R2.Pin_1
  N2: Bauteil1.D4, Keypad4x4.Pin8
  N3: Bauteil1.D5, R3.Pin_0
  N4: Bauteil1.D6, Keypad4x4.Pin7
  N5: Bauteil1.D7, Keypad4x4.Pin6
  N6: Bauteil1.D8, Keypad4x4.Pin5
  N7: Bauteil1.D9, Keypad4x4.Pin4
  N8: Bauteil1.D10, Keypad4x4.Pin3
  N9: Bauteil1.D11/MOSI, Keypad4x4.Pin2
  N10: Bauteil1.D12/MISO, Keypad4x4.Pin1
  VIN: Bauteil1.VIN, Bauteil5.VIN
  5V: Bauteil1.5V, GLCD_128x1.2_Vdd, GLCD_128x1.19_A(+), Bauteil4.VDD
  N11: Bauteil1.A3, R4.Pin_1
  N12: Bauteil1.A2, Bauteil4.IN
  N13: Bauteil1.A1, GLCD_128x1.5_R/W
  N14: Bauteil1.A0, GLCD_128x1.4_D/I
  N15: Bauteil1.D13/SCK, GLCD_128x1.6_Enable
  N16: GLCD_128x1.3_Vo, R2.Pin_0, C1.+
  N17: GLCD_128x1.20_K(-), Q1.C
  N18: Q1.B, R3.Pin_1
  N19: Bauteil5.D1/TX, S1.4
  N20: K1.C2, Q2.C
  N21: Q2.B, R4.Pin_0

notes:
  [24V

custom parts:
  Keypad Membran 4x4: Membrane Keypad 4x4 Matrix
  24 NeoPixel Ring: 24 ultra bright smart LED NeoPixels are arranged in a circle with 2.6" (66mm) outer diameter. The rings are 'chainable' - connect the output pin of one to the input pin of another. Use only one microcontroller pin to control as many as you can chain together! Each LED is addressable as the driver chip is inside the LED. Each one has ~18mA constant current drive so the color will be very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
  PowerBoost 1000 Basic: The PowerBoost 1000 is a little DC/DC boost converter module that can run from 1.8V batteries or higher, and convert the battery output to 5.2V DC for running your 5V projects. At its heart is a TPS61030 boost converter from TI. This boost converter chip has some really nice extras such as low battery detection, 4A internal switch, synchronous conversion, excellent efficiency, and 700KHz high-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

// code stored in the sketch: Lcd_Back_Key.ino

// LCD_128x64_ST7920_DS18B20_DHT11
//
// Dallas DS18B20 temperature sensor on pin 6
// DHT11 relative humidity sensor (humidity only) on pin 8
// display 
// Uses Olikraus' u8g library
// by Floris Wouterlood
// August 11, 2017
// public domain


   #include "U8glib.h"
   #include <OneWire.h>
   #include <DallasTemperature.h>
   #include <DHT.h>

   char temp_string[5]; //empty char array to hold the converted temp float 
   char hum_string[5];  //empty char array to hold the converted humidity float 
   float hum_float;
   int LCD_CONTRAST_PWM_PIN = 3;
   int LCD_BRIGHTNESS_PWM_PIN = 5;
   int contrastValue=0;
   int brightnessValue=0;

// display constructor for u8g library - this one depends on your type of display
  U8GLIB_ST7920_128X64 u8g(13, 11, 14, U8G_PIN_NONE);

// DS18B20 section ================================================================

// one wire data probe to pin 6 
   #define ONE_WIRE_BUS_PIN 6

// Setup a oneWire instance to communicate with any OneWire devices 
   OneWire oneWire(ONE_WIRE_BUS_PIN);
   DallasTemperature sensors(&oneWire);
   DeviceAddress Probe_01 = {0x28, 0xFF, 0x0A, 0x75, 0xA3, 0x15, 0x04, 0xBC}; 
// each DS18B20 has each own unique address - use address finder sketch 


// DHT11 section ==================================================================
// tell the DHT library where to expect a DHT sensor and which type
   DHT DHT_sens(8, DHT11);                //  connected to pin 8 of the Arduino


void setup() {  

//  DHT_sens.begin();                       // start DHT sensoring
//  sensors.begin();                        // START dallas temperature sensoring
//  sensors.setResolution(Probe_01, 10);    // set DS18B20 sensor resolution to 10 bit
  Serial.begin(9600);                     // start serial port 
//  Serial.print("DS18B20 Temperature Control Library Version ");
//  Serial.println(DALLASTEMPLIBVERSION);
  Serial.println ();
//  Serial.println ("DHT11 humidity sensor (temp not implemented)");
//  Serial.print("Number of Devices found on bus = ");  
//  Serial.println(sensors.getDeviceCount());   
  Serial.println ("============================================");
  Serial.print("Getting temperature, humidity... ");  
  Serial.println();  


  // Select font =================================================================
   
  // u8g.setFont(u8g_font_unifont);
  // u8g.setFont(u8g_font_courB10);
  // u8g.setFont(u8g_font_7x14B);
  u8g.setFont(u8g_font_8x13); 

  u8g.setColorIndex(1);                   // Instructs the display to draw with a pixel on. 

  //Declaring backlight pwm pin as output
  pinMode(LCD_BRIGHTNESS_PWM_PIN, OUTPUT);
  pinMode(LCD_CONTRAST_PWM_PIN, OUTPUT);
}

void loop() {  
  
 testFeading();
}

void render(){
  u8g.firstPage();
  do {   
    draw();
  } while( u8g.nextPage() );
}

void testFeading() {
  //Fading the LED
  for(int i=0; i<255; i++){
    changeContrast( i);
    delay(5);
  }
  for(int i=255; i>0; i--){
    changeContrast( i);
    delay(5);
  }
}

void changeContrast(int value){
  contrastValue =value;
  render();
  analogWrite(LCD_CONTRAST_PWM_PIN, 250);
  analogWrite(LCD_BRIGHTNESS_PWM_PIN, value);
}

  
void draw(){


    u8g.drawFrame(0,0,128,31);            // upper frame
    u8g.drawFrame(0,33,128,31);           // lower frame


    float tempC = 32.5;
    float hum_float = 98;

 // convert floats into char u8g strings    
  u8g.drawStr( 15, 13, "Temperature");       // do this for temperature
  dtostrf(tempC, 3, 1, temp_string);
  u8g.drawStr(33,27, temp_string);
  u8g.drawStr(70,27, "*C"); 

  u8g.drawStr(26,45, "Brigthness");             // do this for humidity
  dtostrf(contrastValue, 3, 1, hum_string);
  u8g.drawStr(40,60, hum_string);
 
       

}
